// Logisim project 4bit_comparator.circ as structural Verilog: 1 circuit, main circuit main
module main (
  input  A3,
  input  A2,
  input  A1,
  input  A0,
  input  B3,
  input  B2,
  input  B1,
  input  B0,
  output A_B,
  output A_B_2,
  output A_B_3
);

  wire and_1_out, and_2_out, and_3_out, and_4_out, not_1_out, not_2_out, not_3_out, not_4_out, xnor_1_out,
       xnor_2_out, xnor_3_out, xnor_4_out;

  not not_1 (not_1_out, B3);
  not not_2 (not_2_out, B2);
  not not_3 (not_3_out, B1);
  not not_4 (not_4_out, B0);
  xnor xnor_1 (xnor_1_out, A3, B3);
  xnor xnor_2 (xnor_2_out, A2, B2);
  xnor xnor_3 (xnor_3_out, A1, B1);
  xnor xnor_4 (xnor_4_out, A0, B0);
  and and_1 (and_1_out, A3, not_1_out);
  and and_2 (and_2_out, A2, not_2_out, xnor_1_out);
  and and_3 (and_3_out, A1, not_3_out, xnor_1_out, xnor_2_out);
  and and_4 (and_4_out, A0, xnor_3_out, not_4_out, xnor_1_out, xnor_2_out);
  or or_1 (A_B, and_1_out, and_2_out, and_3_out, and_4_out);
  and and_5 (A_B_2, xnor_1_out, xnor_2_out, xnor_3_out, xnor_4_out);
  nor nor_1 (A_B_3, A_B, A_B_2);
endmodule
